// Logisim project 第5章习题电路的实现.circ as structural Verilog: 13 circuits, main circuit 习题5.4
module \习题5_4  (
  input  x,
  output Z
);

  wire and_1_out, CP_out, j_k_ff_1_q, j_k_ff_2_q, not_1_out;

  Clock #(.highDuration(1), .lowDuration(1)) CP (.out(CP_out));
  not not_1 (not_1_out, x);
  and and_1 (and_1_out, j_k_ff_2_q, x);
  J_K_Flip_Flop #(.trigger("falling"), .Pre_Clr_Positions("ABOVE_BELOW"), .NegatePresetClear("false"), .enable("false"), .NewFFLayout("true")) j_k_ff_1 (
    .J(and_1_out), .clk(CP_out), .K(not_1_out), .Q(j_k_ff_1_q));  // open: Qn, preset, reset
  J_K_Flip_Flop #(.trigger("falling"), .Pre_Clr_Positions("ABOVE_BELOW"), .NegatePresetClear("false"), .enable("false"), .NewFFLayout("true")) j_k_ff_2 (
    .J(x), .clk(CP_out), .K(not_1_out), .Q(j_k_ff_2_q));  // open: Qn, preset, reset
  and and_2 (Z, j_k_ff_1_q, x, j_k_ff_2_q);

  // Notes on the sheet:
  //   y2
  //   y1
endmodule

module \习题5_5  (
  input  x,
  output y2,
  output Z,
  output y1
);

  wire and_1_out, and_2_out, and_3_out, and_4_out, CP_out, d_ff_1_qn, d_ff_2_qn, nand_1_out, not_1_out,
       or_1_out, xor_1_out;

  Clock #(.highDuration(1), .lowDuration(1)) CP (.out(CP_out));
  not not_1 (not_1_out, x);
  xor xor_1 (xor_1_out, x, y2);
  and and_1 (and_1_out, d_ff_2_qn, x);
  or or_1 (or_1_out, and_1_out, and_2_out);
  and and_2 (and_2_out, not_1_out, y1, d_ff_1_qn);
  nand nand_1 (nand_1_out, y1, xor_1_out);
  D_Flip_Flop #(.trigger("rising"), .Pre_Clr_Positions("ABOVE_BELOW"), .NegatePresetClear("false"), .enable("false"), .NewFFLayout("true")) d_ff_1 (
    .clk(CP_out), .D(or_1_out), .Q(y2), .Qn(d_ff_1_qn));  // open: preset, reset
  D_Flip_Flop #(.trigger("rising"), .Pre_Clr_Positions("ABOVE_BELOW"), .NegatePresetClear("false"), .enable("false"), .NewFFLayout("true")) d_ff_2 (
    .clk(CP_out), .D(nand_1_out), .Q(y1), .Qn(d_ff_2_qn));  // open: preset, reset
  and and_3 (and_3_out, y2, y1, not_1_out);
  or or_2 (Z, and_3_out, and_4_out);
  and and_4 (and_4_out, d_ff_2_qn, d_ff_1_qn, x);
endmodule

module \习题5_6  (
  input  x,
  output y2,
  output Z,
  output y1
);

  wire and_1_out, and_2_out, CP_out, j_k_ff_1_qn, j_k_ff_2_qn, not_1_out, xor_1_out;

  Clock #(.highDuration(1), .lowDuration(1)) CP (.out(CP_out));
  xor xor_1 (xor_1_out, y1, x);
  not not_1 (not_1_out, x);
  J_K_Flip_Flop #(.trigger("falling"), .Pre_Clr_Positions("ABOVE_BELOW"), .NegatePresetClear("false"), .enable("false"), .NewFFLayout("true")) j_k_ff_1 (
    .J(xor_1_out), .clk(CP_out), .K(xor_1_out), .Q(y2), .Qn(j_k_ff_1_qn));  // open: preset, reset
  J_K_Flip_Flop #(.trigger("falling"), .Pre_Clr_Positions("ABOVE_BELOW"), .NegatePresetClear("false"), .enable("false"), .NewFFLayout("true")) j_k_ff_2 (
    .J(1'b1), .clk(CP_out), .K(1'b1), .Q(y1), .Qn(j_k_ff_2_qn));  // open: preset, reset
  and and_1 (and_1_out, x, j_k_ff_2_qn, j_k_ff_1_qn);
  and and_2 (and_2_out, y2, not_1_out, y1);
  or or_1 (Z, and_1_out, and_2_out);
endmodule

module \习题5_8  (
  input  X,
  output y4,
  output y3,
  output Z,
  output y2,
  output y1
);

  wire CP_out, or_1_out;

  Clock #(.highDuration(1), .lowDuration(1)) CP (.out(CP_out));
  D_Flip_Flop #(.trigger("rising"), .Pre_Clr_Positions("ABOVE_BELOW"), .NegatePresetClear("false"), .enable("false"), .NewFFLayout("true")) d_ff_1 (
    .clk(CP_out), .D(y3), .Q(y4));  // open: Qn, preset, reset
  D_Flip_Flop #(.trigger("rising"), .Pre_Clr_Positions("ABOVE_BELOW"), .NegatePresetClear("false"), .enable("false"), .NewFFLayout("true")) d_ff_2 (
    .clk(CP_out), .D(y2), .Q(y3));  // open: Qn, preset, reset
  D_Flip_Flop #(.trigger("rising"), .Pre_Clr_Positions("ABOVE_BELOW"), .NegatePresetClear("false"), .enable("false"), .NewFFLayout("true")) d_ff_3 (
    .clk(CP_out), .D(y1), .Q(y2));  // open: Qn, preset, reset
  D_Flip_Flop #(.trigger("rising"), .Pre_Clr_Positions("ABOVE_BELOW"), .NegatePresetClear("false"), .enable("false"), .NewFFLayout("true")) d_ff_4 (
    .clk(CP_out), .D(X), .Q(y1));  // open: Qn, preset, reset
  or or_1 (or_1_out, y3, y2);
  and and_1 (Z, y4, or_1_out);
endmodule

module \习题5_8的仿真  (
  output y4,
  output y3,
  output Z,
  output y2,
  output y1,
  output Z_2
);

  wire button_1_out, comparator_1_eq, CP, not_1_out, or_1_out, rom_1_data;
  wire [5:0] counter_1_q;

  Clock #(.highDuration(1), .lowDuration(1)) u_CP (.out(CP));
  Button button_1 (.out(button_1_out));
  Counter #(.width(6), .max('h3f), .ongoal("wrap"), .trigger("rising"), .behavior("new")) counter_1 (
    .Q(counter_1_q), .clk(CP), .clr(button_1_out));  // open: load, D, count, carry, preset, down
  // Probe on rom_1_data
  ROM #(.addrWidth(6), .dataWidth(1), .Select("low")) rom_1 (.addr(counter_1_q), .data(rom_1_data));
  D_Flip_Flop #(.trigger("rising"), .Pre_Clr_Positions("ABOVE_BELOW"), .NegatePresetClear("false"), .enable("false"), .NewFFLayout("true")) d_ff_1 (
    .clk(CP), .D(y3), .Q(y4));  // open: Qn, preset, reset
  D_Flip_Flop #(.trigger("rising"), .Pre_Clr_Positions("ABOVE_BELOW"), .NegatePresetClear("false"), .enable("false"), .NewFFLayout("true")) d_ff_2 (
    .clk(CP), .D(y2), .Q(y3));  // open: Qn, preset, reset
  D_Flip_Flop #(.trigger("rising"), .Pre_Clr_Positions("ABOVE_BELOW"), .NegatePresetClear("false"), .enable("false"), .NewFFLayout("true")) d_ff_3 (
    .clk(CP), .D(y1), .Q(y2));  // open: Qn, preset, reset
  D_Flip_Flop #(.trigger("rising"), .Pre_Clr_Positions("ABOVE_BELOW"), .NegatePresetClear("false"), .enable("false"), .NewFFLayout("true")) d_ff_4 (
    .clk(CP), .D(rom_1_data), .Q(y1));  // open: Qn, preset, reset
  or or_1 (or_1_out, y3, y2);
  ROM #(.addrWidth(4), .dataWidth(1), .Select("low")) rom_2 (.addr({y4, y3, y2, y1}), .data(Z_2));
  and and_1 (Z, y4, or_1_out);
  Comparator #(.width(1), .mode("twosComplement")) comparator_1 (.a(Z), .b(Z_2), .eq(comparator_1_eq));  // open: gt, lt
  not not_1 (not_1_out, comparator_1_eq);
  // Buzzer #(.freq_measure("Hz"), .vol_width(7)) buzzer_1: pin names not known; wires that end beside it: not_1_out
  LED #(.active("false")) led_1 (.in(comparator_1_eq));

  // Notes on the sheet:
  //   contents of rom_1 (hex, n*v repeats v):
  //   7*0 1 0 0 1 0 0 0 1 1 0 1 0 0 0 1 0 1 0 1 1 0 0 4*1 0 0 0 1 0 0 1 1 0 1 0 1 0 4*1 0 0 1 1 0 4*1 0
  //   4*1
  //   ROM1
  //   ROM2
  //   contents of rom_2 (hex, n*v repeats v):
  //   10*0 6*1
endmodule

module \习题5_12  (
  input  x,
  input  x_2,
  input  x_3,
  output y2,
  output Z,
  output y1,
  output y2_2,
  output Z_2,
  output y1_2,
  output y2_3,
  output Z_3,
  output y1_3
);

  wire and_1_out, and_2_out, and_3_out, and_4_out, and_5_out, and_6_out, and_7_out, and_8_out, and_9_out,
       CP_2_out, CP_3_out, CP_out, d_ff_1_qn, d_ff_2_qn, j_k_ff_1_qn, j_k_ff_2_qn, not_1_out, not_2_out,
       not_3_out, or_1_out, or_2_out, or_3_out, or_4_out, or_5_out, or_6_out, or_7_out, t_ff_1_qn, t_ff_2_qn,
       xor_1_out, xor_2_out, xor_3_out, xor_4_out, xor_5_out;

  Clock #(.highDuration(1), .lowDuration(1)) CP (.out(CP_out));
  Clock #(.highDuration(1), .lowDuration(1)) CP_2 (.out(CP_2_out));
  Clock #(.highDuration(1), .lowDuration(1)) CP_3 (.out(CP_3_out));
  not not_1 (not_1_out, x);
  not not_2 (not_2_out, x_2);
  not not_3 (not_3_out, x_3);
  and and_1 (and_1_out, d_ff_1_qn, x);
  xor xor_1 (xor_1_out, y1, x);
  and and_2 (and_2_out, y2_2, t_ff_2_qn, not_2_out);
  and and_3 (and_3_out, x_2, y1_2);
  and and_4 (and_4_out, y1_2, t_ff_1_qn);
  and and_5 (and_5_out, t_ff_1_qn, x_2);
  and and_6 (and_6_out, not_2_out, t_ff_1_qn, t_ff_2_qn);
  and and_7 (and_7_out, x_2, y2_2, t_ff_2_qn);
  and and_8 (and_8_out, not_2_out, y1_2, y2_2);
  and and_9 (and_9_out, x_2, t_ff_1_qn, y1_2);
  or or_1 (or_1_out, and_1_out, xor_1_out);
  xor xor_2 (xor_2_out, d_ff_1_qn, x);
  or or_2 (or_2_out, and_2_out, and_3_out, and_4_out, and_5_out);
  or or_3 (or_3_out, and_6_out, and_7_out, and_8_out, and_9_out);
  or or_4 (or_4_out, x_3, y1_3);
  xor xor_3 (xor_3_out, x_3, j_k_ff_2_qn);
  xor xor_4 (xor_4_out, x_3, j_k_ff_1_qn);
  xor xor_5 (xor_5_out, x_3, y2_3);
  D_Flip_Flop #(.trigger("rising"), .Pre_Clr_Positions("ABOVE_BELOW"), .NegatePresetClear("false"), .enable("false"), .NewFFLayout("true")) d_ff_1 (
    .clk(CP_out), .D(or_1_out), .Q(y2), .Qn(d_ff_1_qn));  // open: preset, reset
  D_Flip_Flop #(.trigger("rising"), .Pre_Clr_Positions("ABOVE_BELOW"), .NegatePresetClear("false"), .enable("false"), .NewFFLayout("true")) d_ff_2 (
    .clk(CP_out), .D(xor_2_out), .Q(y1), .Qn(d_ff_2_qn));  // open: preset, reset
  T_Flip_Flop #(.trigger("rising"), .Pre_Clr_Positions("ABOVE_BELOW"), .NegatePresetClear("false"), .enable("false"), .NewFFLayout("true")) t_ff_1 (
    .clk(CP_2_out), .T(or_2_out), .Q(y2_2), .Qn(t_ff_1_qn));  // open: preset, reset
  T_Flip_Flop #(.trigger("rising"), .Pre_Clr_Positions("ABOVE_BELOW"), .NegatePresetClear("false"), .enable("false"), .NewFFLayout("true")) t_ff_2 (
    .clk(CP_2_out), .T(or_3_out), .Q(y1_2), .Qn(t_ff_2_qn));  // open: preset, reset
  J_K_Flip_Flop #(.trigger("rising"), .Pre_Clr_Positions("ABOVE_BELOW"), .NegatePresetClear("false"), .enable("false"), .NewFFLayout("true")) j_k_ff_1 (
    .J(or_4_out), .clk(CP_3_out), .K(xor_3_out), .Q(y2_3), .Qn(j_k_ff_1_qn));  // open: preset, reset
  J_K_Flip_Flop #(.trigger("rising"), .Pre_Clr_Positions("ABOVE_BELOW"), .NegatePresetClear("false"), .enable("false"), .NewFFLayout("true")) j_k_ff_2 (
    .J(xor_4_out), .clk(CP_3_out), .K(xor_5_out), .Q(y1_3), .Qn(j_k_ff_2_qn));  // open: preset, reset
  or or_5 (or_5_out, not_1_out, d_ff_2_qn);
  or or_6 (or_6_out, not_2_out, t_ff_2_qn);
  or or_7 (or_7_out, not_3_out, j_k_ff_2_qn);
  and and_10 (Z, y2, or_5_out);
  and and_11 (Z_2, y2_2, or_6_out);
  and and_12 (Z_3, y2_3, or_7_out);
endmodule

module \习题5_12的仿真  (
  input  x,
  output y2,
  output Z,
  output y1,
  output y2_2,
  output Z_2,
  output y1_2,
  output y2_3,
  output Z_3,
  output y1_3
);

  wire and_1_out, and_2_out, and_3_out, and_4_out, and_5_out, and_6_out, and_7_out, and_8_out, and_9_out,
       comparator_1_eq, comparator_2_eq, CP, d_ff_1_qn, d_ff_2_qn, j_k_ff_1_qn, j_k_ff_2_qn, not_1_out,
       not_2_out, not_3_out, not_4_out, not_5_out, or_1_out, or_2_out, or_3_out, or_4_out, or_5_out,
       or_6_out, or_7_out, t_ff_1_qn, t_ff_2_qn, xor_1_out, xor_2_out, xor_3_out, xor_4_out, xor_5_out;

  Clock #(.highDuration(1), .lowDuration(1)) u_CP (.out(CP));
  not not_1 (not_1_out, x);
  not not_2 (not_2_out, x);
  not not_3 (not_3_out, x);
  and and_1 (and_1_out, d_ff_1_qn, x);
  xor xor_1 (xor_1_out, y1, x);
  and and_2 (and_2_out, y2_2, t_ff_2_qn, not_2_out);
  and and_3 (and_3_out, x, y1_2);
  and and_4 (and_4_out, y1_2, t_ff_1_qn);
  and and_5 (and_5_out, t_ff_1_qn, x);
  and and_6 (and_6_out, not_2_out, t_ff_1_qn, t_ff_2_qn);
  and and_7 (and_7_out, x, y2_2, t_ff_2_qn);
  and and_8 (and_8_out, not_2_out, y1_2, y2_2);
  and and_9 (and_9_out, x, t_ff_1_qn, y1_2);
  or or_1 (or_1_out, and_1_out, xor_1_out);
  xor xor_2 (xor_2_out, d_ff_1_qn, x);
  or or_2 (or_2_out, and_2_out, and_3_out, and_4_out, and_5_out);
  or or_3 (or_3_out, and_6_out, and_7_out, and_8_out, and_9_out);
  or or_4 (or_4_out, x, y1_3);
  xor xor_3 (xor_3_out, x, j_k_ff_2_qn);
  xor xor_4 (xor_4_out, x, j_k_ff_1_qn);
  xor xor_5 (xor_5_out, x, y2_3);
  D_Flip_Flop #(.trigger("rising"), .Pre_Clr_Positions("ABOVE_BELOW"), .NegatePresetClear("false"), .enable("false"), .NewFFLayout("true")) d_ff_1 (
    .clk(CP), .D(or_1_out), .Q(y2), .Qn(d_ff_1_qn));  // open: preset, reset
  D_Flip_Flop #(.trigger("rising"), .Pre_Clr_Positions("ABOVE_BELOW"), .NegatePresetClear("false"), .enable("false"), .NewFFLayout("true")) d_ff_2 (
    .clk(CP), .D(xor_2_out), .Q(y1), .Qn(d_ff_2_qn));  // open: preset, reset
  T_Flip_Flop #(.trigger("rising"), .Pre_Clr_Positions("ABOVE_BELOW"), .NegatePresetClear("false"), .enable("false"), .NewFFLayout("true")) t_ff_1 (
    .clk(CP), .T(or_2_out), .Q(y2_2), .Qn(t_ff_1_qn));  // open: preset, reset
  T_Flip_Flop #(.trigger("rising"), .Pre_Clr_Positions("ABOVE_BELOW"), .NegatePresetClear("false"), .enable("false"), .NewFFLayout("true")) t_ff_2 (
    .clk(CP), .T(or_3_out), .Q(y1_2), .Qn(t_ff_2_qn));  // open: preset, reset
  J_K_Flip_Flop #(.trigger("rising"), .Pre_Clr_Positions("ABOVE_BELOW"), .NegatePresetClear("false"), .enable("false"), .NewFFLayout("true")) j_k_ff_1 (
    .J(or_4_out), .clk(CP), .K(xor_3_out), .Q(y2_3), .Qn(j_k_ff_1_qn));  // open: preset, reset
  J_K_Flip_Flop #(.trigger("rising"), .Pre_Clr_Positions("ABOVE_BELOW"), .NegatePresetClear("false"), .enable("false"), .NewFFLayout("true")) j_k_ff_2 (
    .J(xor_4_out), .clk(CP), .K(xor_5_out), .Q(y1_3), .Qn(j_k_ff_2_qn));  // open: preset, reset
  or or_5 (or_5_out, not_1_out, d_ff_2_qn);
  or or_6 (or_6_out, not_2_out, t_ff_2_qn);
  or or_7 (or_7_out, not_3_out, j_k_ff_2_qn);
  and and_10 (Z, y2, or_5_out);
  and and_11 (Z_2, y2_2, or_6_out);
  and and_12 (Z_3, y2_3, or_7_out);
  Comparator #(.width(3), .mode("twosComplement")) comparator_1 (
    .a({y1, Z, y2}), .b({y1_2, Z_2, y2_2}), .eq(comparator_1_eq));  // open: gt, lt
  Comparator #(.width(3), .mode("twosComplement")) comparator_2 (
    .a({y1_2, Z_2, y2_2}), .b({y1_3, Z_3, y2_3}), .eq(comparator_2_eq));  // open: gt, lt
  not not_4 (not_4_out, comparator_1_eq);
  // Buzzer #(.freq_measure("Hz"), .vol_width(7)) buzzer_1: pin names not known; wires that end beside it: not_4_out
  LED #(.active("false")) led_1 (.in(comparator_1_eq));
  not not_5 (not_5_out, comparator_2_eq);
  // Buzzer #(.freq_measure("Hz"), .vol_width(7)) buzzer_2: pin names not known; wires that end beside it: not_5_out
  LED #(.active("false")) led_2 (.in(comparator_2_eq));
endmodule

module \习题5_13  (
  input  x,
  input  x_2,
  output y2,
  output Z,
  output y1,
  output y2_2,
  output Z_2,
  output y1_2
);

  wire and_1_out, and_2_out, and_3_out, and_4_out, and_5_out, CP_2_out, CP_out, d_ff_1_qn, d_ff_2_qn,
       j_k_ff_1_qn, j_k_ff_2_qn, not_1_out, or_1_out, or_2_out, or_3_out, xor_1_out, xor_2_out, xor_3_out;

  Clock #(.highDuration(1), .lowDuration(1)) CP (.out(CP_out));
  Clock #(.highDuration(1), .lowDuration(1)) CP_2 (.out(CP_2_out));
  not not_1 (not_1_out, x);
  and and_1 (and_1_out, not_1_out, y2);
  and and_2 (and_2_out, y2, d_ff_2_qn, x);
  and and_3 (and_3_out, not_1_out, y2);
  and and_4 (and_4_out, y2, d_ff_2_qn);
  and and_5 (and_5_out, x, d_ff_1_qn, y1);
  or or_1 (or_1_out, x_2, y1_2);
  or or_2 (or_2_out, and_1_out, and_2_out);
  or or_3 (or_3_out, and_3_out, and_4_out, and_5_out);
  xor xor_1 (xor_1_out, x_2, j_k_ff_2_qn);
  xor xor_2 (xor_2_out, x_2, j_k_ff_1_qn);
  xor xor_3 (xor_3_out, x_2, y2_2);
  D_Flip_Flop #(.trigger("rising"), .Pre_Clr_Positions("ABOVE_BELOW"), .NegatePresetClear("false"), .enable("false"), .NewFFLayout("true")) d_ff_1 (
    .clk(CP_out), .D(or_2_out), .Q(y2), .Qn(d_ff_1_qn));  // open: preset, reset
  D_Flip_Flop #(.trigger("rising"), .Pre_Clr_Positions("ABOVE_BELOW"), .NegatePresetClear("false"), .enable("false"), .NewFFLayout("true")) d_ff_2 (
    .clk(CP_out), .D(or_3_out), .Q(y1), .Qn(d_ff_2_qn));  // open: preset, reset
  J_K_Flip_Flop #(.trigger("rising"), .Pre_Clr_Positions("ABOVE_BELOW"), .NegatePresetClear("false"), .enable("false"), .NewFFLayout("true")) j_k_ff_1 (
    .J(or_1_out), .clk(CP_2_out), .K(xor_1_out), .Q(y2_2), .Qn(j_k_ff_1_qn));  // open: preset, reset
  J_K_Flip_Flop #(.trigger("rising"), .Pre_Clr_Positions("ABOVE_BELOW"), .NegatePresetClear("false"), .enable("false"), .NewFFLayout("true")) j_k_ff_2 (
    .J(xor_2_out), .clk(CP_2_out), .K(xor_3_out), .Q(y1_2), .Qn(j_k_ff_2_qn));  // open: preset, reset

  assign Z = y2;
  assign Z_2 = y2_2;
endmodule

module \习题5_14_1  (
  input  X,
  input  Y,
  output Zx,
  output Zy
);

  wire and_1_out, and_2_out, CP_out, j_k_ff_1_q, j_k_ff_2_q, not_1_out, not_2_out, or_1_out, or_2_out;

  Clock #(.highDuration(1), .lowDuration(1)) CP (.out(CP_out));
  not not_1 (not_1_out, X);
  not not_2 (not_2_out, Y);
  and and_1 (and_1_out, X, Zx, not_2_out);
  or or_1 (or_1_out, Zy, j_k_ff_2_q);
  and and_2 (and_2_out, not_1_out, Y, Zy);
  or or_2 (or_2_out, Zx, j_k_ff_1_q);
  J_K_Flip_Flop #(.trigger("rising"), .Pre_Clr_Positions("ABOVE_BELOW"), .NegatePresetClear("false"), .enable("false"), .NewFFLayout("true")) j_k_ff_1 (
    .J(and_1_out), .clk(CP_out), .K(or_1_out), .Q(j_k_ff_1_q), .Qn(Zy));  // open: preset, reset
  J_K_Flip_Flop #(.trigger("rising"), .Pre_Clr_Positions("ABOVE_BELOW"), .NegatePresetClear("false"), .enable("false"), .NewFFLayout("true")) j_k_ff_2 (
    .J(and_2_out), .clk(CP_out), .K(or_2_out), .Q(j_k_ff_2_q), .Qn(Zx));  // open: preset, reset

  // Notes on the sheet:
  //   y2
  //   y1
endmodule

module \习题5_14_1_的仿真  (
  input  in_1,
  output Zx,
  output Zy
);

  wire and_1_out, and_2_out, CP, j_k_ff_1_q, j_k_ff_2_q, not_1_out, not_2_out, or_1_out, or_2_out, X, Y;

  Clock #(.highDuration(1), .lowDuration(1)) u_CP (.out(CP));
  not not_1 (not_1_out, X);
  not not_2 (not_2_out, Y);
  // Digital_Oscilloscope #(.nState(15), .frontlines("rising"), .showclock("true")) digital_oscilloscope_1: pin names not known; wires that end beside it: CP, X, Y, Zx, Zy
  Shift_Register #(.width(1), .length(8), .parallel("true"), .trigger("rising")) shift_register_1 (
    .shift(1'b1), .in(1'b0), .clk(CP), .out(X), .load(in_1), .clr(1'b0), .d0(1'b1), .d1(1'b1), .d2(1'b0),
    .d3(1'b0), .d4(1'b1), .d5(1'b0), .d6(1'b1), .d7(1'b0));  // open: q0, q1, q2, q3, q4, q5, q6, q7
  and and_1 (and_1_out, X, Zx, not_2_out);
  or or_1 (or_1_out, Zy, j_k_ff_2_q);
  and and_2 (and_2_out, not_1_out, Y, Zy);
  or or_2 (or_2_out, Zx, j_k_ff_1_q);
  J_K_Flip_Flop #(.trigger("rising"), .Pre_Clr_Positions("ABOVE_BELOW"), .NegatePresetClear("false"), .enable("false"), .NewFFLayout("true")) j_k_ff_1 (
    .J(and_1_out), .clk(CP), .K(or_1_out), .Q(j_k_ff_1_q), .Qn(Zy));  // open: preset, reset
  J_K_Flip_Flop #(.trigger("rising"), .Pre_Clr_Positions("ABOVE_BELOW"), .NegatePresetClear("false"), .enable("false"), .NewFFLayout("true")) j_k_ff_2 (
    .J(and_2_out), .clk(CP), .K(or_2_out), .Q(j_k_ff_2_q), .Qn(Zx));  // open: preset, reset
  Shift_Register #(.width(1), .length(8), .parallel("true"), .trigger("rising")) shift_register_2 (
    .shift(1'b1), .in(1'b0), .clk(CP), .out(Y), .load(in_1), .clr(1'b0), .d0(1'b1), .d1(1'b0), .d2(1'b1),
    .d3(1'b0), .d4(1'b1), .d5(1'b0), .d6(1'b1), .d7(1'b0));  // open: q0, q1, q2, q3, q4, q5, q6, q7

  // Other names for the same wires on the sheet: Load = in_1

  // Notes on the sheet:
  //   y2
  //   y1
endmodule

module \习题5_14_2  (
  input  X,
  input  Y,
  output Zx,
  output Zy
);

  wire and_1_out, and_2_out, and_3_out, and_4_out, CP_out, j_k_ff_1_q, j_k_ff_2_q, not_1_out, not_2_out,
       or_1_out, or_2_out;

  Clock #(.highDuration(1), .lowDuration(1)) CP (.out(CP_out));
  not not_1 (not_1_out, X);
  not not_2 (not_2_out, Y);
  or or_1 (or_1_out, not_1_out, Y);
  or or_2 (or_2_out, X, not_2_out);
  and and_1 (and_1_out, X, Zx, not_2_out);
  and and_2 (and_2_out, or_1_out, j_k_ff_2_q);
  and and_3 (and_3_out, not_1_out, Y, Zy);
  and and_4 (and_4_out, or_2_out, j_k_ff_1_q);
  J_K_Flip_Flop #(.trigger("rising"), .Pre_Clr_Positions("ABOVE_BELOW"), .NegatePresetClear("false"), .enable("false"), .NewFFLayout("true")) j_k_ff_1 (
    .J(and_1_out), .clk(CP_out), .K(and_2_out), .Q(j_k_ff_1_q), .Qn(Zy));  // open: preset, reset
  J_K_Flip_Flop #(.trigger("rising"), .Pre_Clr_Positions("ABOVE_BELOW"), .NegatePresetClear("false"), .enable("false"), .NewFFLayout("true")) j_k_ff_2 (
    .J(and_3_out), .clk(CP_out), .K(and_4_out), .Q(j_k_ff_2_q), .Qn(Zx));  // open: preset, reset

  // Notes on the sheet:
  //   y2
  //   y1
endmodule

module \习题5_14_2_的仿真  (
  input  in_1,
  output Zx,
  output Zy
);

  wire and_1_out, and_2_out, and_3_out, and_4_out, CP, j_k_ff_1_q, j_k_ff_2_q, not_1_out, not_2_out,
       or_1_out, or_2_out, X, Y;

  Clock #(.highDuration(1), .lowDuration(1)) u_CP (.out(CP));
  not not_1 (not_1_out, X);
  not not_2 (not_2_out, Y);
  Shift_Register #(.width(1), .length(8), .parallel("true"), .trigger("rising")) shift_register_1 (
    .shift(1'b1), .in(1'b0), .clk(CP), .out(X), .load(in_1), .clr(1'b0), .d0(1'b1), .d1(1'b1), .d2(1'b0),
    .d3(1'b0), .d4(1'b1), .d5(1'b0), .d6(1'b1), .d7(1'b0));  // open: q0, q1, q2, q3, q4, q5, q6, q7
  // Digital_Oscilloscope #(.nState(15), .frontlines("rising"), .showclock("true")) digital_oscilloscope_1: pin names not known; wires that end beside it: CP, X, Y, Zx, Zy
  or or_1 (or_1_out, not_1_out, Y);
  or or_2 (or_2_out, X, not_2_out);
  and and_1 (and_1_out, X, Zx, not_2_out);
  and and_2 (and_2_out, or_1_out, j_k_ff_2_q);
  and and_3 (and_3_out, not_1_out, Y, Zy);
  and and_4 (and_4_out, or_2_out, j_k_ff_1_q);
  J_K_Flip_Flop #(.trigger("rising"), .Pre_Clr_Positions("ABOVE_BELOW"), .NegatePresetClear("false"), .enable("false"), .NewFFLayout("true")) j_k_ff_1 (
    .J(and_1_out), .clk(CP), .K(and_2_out), .Q(j_k_ff_1_q), .Qn(Zy));  // open: preset, reset
  J_K_Flip_Flop #(.trigger("rising"), .Pre_Clr_Positions("ABOVE_BELOW"), .NegatePresetClear("false"), .enable("false"), .NewFFLayout("true")) j_k_ff_2 (
    .J(and_3_out), .clk(CP), .K(and_4_out), .Q(j_k_ff_2_q), .Qn(Zx));  // open: preset, reset
  Shift_Register #(.width(1), .length(8), .parallel("true"), .trigger("rising")) shift_register_2 (
    .shift(1'b1), .in(1'b0), .clk(CP), .out(Y), .load(in_1), .clr(1'b0), .d0(1'b1), .d1(1'b0), .d2(1'b1),
    .d3(1'b0), .d4(1'b1), .d5(1'b0), .d6(1'b1), .d7(1'b0));  // open: q0, q1, q2, q3, q4, q5, q6, q7

  // Other names for the same wires on the sheet: Load = in_1

  // Notes on the sheet:
  //   y2
  //   y1
endmodule

module \习题5_15  (
  output y4,
  output y3,
  output y2,
  output y1
);

  wire and_1_out, and_2_out, and_3_out, and_4_out, clock_1_out, not_1_out, or_1_out;

  Clock #(.highDuration(1), .lowDuration(1)) clock_1 (.out(clock_1_out));
  and and_1 (and_1_out, y4, y1);
  and and_2 (and_2_out, y3, y2, y1);
  not not_1 (not_1_out, y4);
  or or_1 (or_1_out, and_1_out, and_2_out);
  and and_3 (and_3_out, y2, y1);
  and and_4 (and_4_out, not_1_out, y1);
  T_Flip_Flop #(.trigger("rising"), .Pre_Clr_Positions("ABOVE_BELOW"), .NegatePresetClear("false"), .enable("false"), .NewFFLayout("true")) t_ff_1 (
    .clk(clock_1_out), .T(or_1_out), .Q(y4));  // open: Qn, preset, reset
  T_Flip_Flop #(.trigger("rising"), .Pre_Clr_Positions("ABOVE_BELOW"), .NegatePresetClear("false"), .enable("false"), .NewFFLayout("true")) t_ff_2 (
    .clk(clock_1_out), .T(and_3_out), .Q(y3));  // open: Qn, preset, reset
  T_Flip_Flop #(.trigger("rising"), .Pre_Clr_Positions("ABOVE_BELOW"), .NegatePresetClear("false"), .enable("false"), .NewFFLayout("true")) t_ff_3 (
    .clk(clock_1_out), .T(and_4_out), .Q(y2));  // open: Qn, preset, reset
  T_Flip_Flop #(.trigger("rising"), .Pre_Clr_Positions("ABOVE_BELOW"), .NegatePresetClear("false"), .enable("false"), .NewFFLayout("true")) t_ff_4 (
    .clk(clock_1_out), .T(1'b1), .Q(y1));  // open: Qn, preset, reset
  // Probe on {y4, y3, y2, y1}
  // Probe on {y4, y3, y2, y1}
endmodule
